# Fritzing sketch FE (saved by Fritzing 0.9.10b)
breadboards: 1

parts:
  L298N2 = L298N DC motor driver
  Bauteil1 = Adafruit Proto Shield for Arduino Kit - v.5
  S1 = Tilt Switch [package=THT]
  M1 = DC Motor [voltage_(max)=6V voltage_(min)=3V]
  J1 = Basic Servo
  HC-SR04_Sensor_1 = HC-SR04 Ultrasonic Distance Sensor
  HC-SR04_Sensor_2 = HC-SR04 Ultrasonic Distance Sensor
  U1 = TRANSCHIPTC5747 [package=camera_sfv24r-2st_2]  # not connected
  VCC1 = Battery
  Bauteil2 = Arduino Uno (Rev3)  # not connected
  HC-SR04_Sensor_3 = HC-SR04 Ultrasonic Distance Sensor

nets:
  N1: L298N2.OUT1, M1.pin_2
  N2: L298N2.OUT2, M1.pin_1
  N3: L298N2.OUT3, J1.vcc
  N4: L298N2.OUT4, J1.gnd
  N5: L298N2.12V, VCC1.+
  GND: L298N2.GND, Bauteil1.GND, S1.Pin_1, HC-SR04_Sensor_1.GND, HC-SR04_Sensor_2.GND, HC-SR04_Sensor_3.GND
  VCC: L298N2.5V, L298N2.IN1, L298N2.IN4, Bauteil1.+5V, HC-SR04_Sensor_1.VCC, HC-SR04_Sensor_2.VCC, HC-SR04_Sensor_3.VCC
  N6: L298N2.ENA, Bauteil1.D11
  N7: Bauteil1.D9, J1.pulse
  N8: Bauteil1.D2, HC-SR04_Sensor_3.ECHO
  N9: Bauteil1.D3, HC-SR04_Sensor_3.TRIG
  N10: Bauteil1.D4, HC-SR04_Sensor_1.ECHO
  N11: Bauteil1.D5, HC-SR04_Sensor_1.TRIG
  N12: Bauteil1.D6, HC-SR04_Sensor_2.ECHO
  N13: Bauteil1.D7, HC-SR04_Sensor_2.TRIG
  N14: S1.Pin_2, VCC1.-

custom parts:
  L298N DC motor driver: 2x DC motor driver with 78M05 positive voltage regulator (7..35 V) L298N: max 46 V, 2 A Set 5 V Enable jumper to enable 5 V regultor (needed for the L298N) and +5 V output at screw terminal or supply external +5 V at screw terminal Set ENA and/or ENB to +5 V to enable motor permanently or supply ENA and/or ENB with PWM signal IN1 and IN2 set rotation directory for motor A (OUT1/OUT2) IN2 and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
  Adafruit Proto Shield for Arduino Kit - v.5: Arduino prototyping shield designed by Adafruit Industries

// code stored in the sketch: RC_Control.ino
#include "variables.h" // all the vars, actuators, and sensors are defined and initialized here.
#include "ControlRC.h" // all functions for control, read sonsor and update variables are located here  



void setup() {
  initializeHardware();
}

void loop() {
  
 //drive();
 updateDistanceData();
 manager.printDistances();
 delay(10);
}
